# Fritzing sketch FanInterFace (saved by Fritzing 0.9.3b)
breadboards: 1

parts:
  Part1 = Arduino Pro Mini v13 [part_number="Arduino Pro Mni 3.3V"]
  U1 = V_REG_LD1117VXX [part_number="AMS1117 3.3V" package=78xxl]
  R1 = Resistor [tolerance=±5% resistance=150 package=THT]
  R2 = Resistor [tolerance=±5% resistance=100k package=THT]
  D1 = Diode [part_number=1N4148 package=diode-1n4148]
  J1 = female pin header, 3 pins [form="♀ (female)" part_number="To Fan Controller"]
  J2 = male pin header, 3 pins [form="♂ (male)" part_number="3pin Fan"]
  J3 = male pin header, 3 pins [form="♂ (male)" part_number="2pin Fan"]
  Q1 = MOSFET-NCHANNEL [part_number=2N7000 package=to-92]

nets:
  N1: Part1.VCC, U1.OUT
  N2: Part1.D5_PWM, R1.Pin_0
  N3: Part1.D4, D1.A
  GND: Part1.GND, U1.GND, R2.Pin_0, J1.pin1, J2.pin1, J3.pin1, Q1.S
  N4: U1.IN, J1.pin3, J2.pin3, J3.pin3
  N5: R1.Pin_1, R2.Pin_1, Q1.G
  N6: D1.C, J2.pin2
  N7: J1.pin2, Q1.D
